# Fritzing sketch Babysoon (saved by Fritzing 0.9.3b)
circuit board: 8.46667cm x 5.64444cm
breadboards: 1

parts:
  Q1 = NPN-Transistor [package="TO92 [THT]"]
  ESP1 = ESP32 DOIT DEV KIT V1 [package="DIP (Dual Inline)"]
  Dev1 = GY-NEO6MV2 [package=SIP]
  Dev2 = SSD1306I2C [package=SIP]
  Dev3 = MPU9265 [package=SIP]
  R1 = Resistor [tolerance=±5% resistance=220 package=THT]

nets:
  N1: Q1.E, Q1.C, ESP1.pin_29, Dev1.pin4, Dev2.pin1, Dev3.pin2
  N2: Q1.B, R1.Pin_0
  N3: ESP1.pin_17, Dev2.pin3, Dev3.pin3
  N4: ESP1.pin_20, Dev2.pin4, Dev3.pin4
  N5: ESP1.pin_23, R1.Pin_1
  N6: ESP1.pin_25, Dev1.pin2
  N7: ESP1.pin_26, Dev1.pin3
  N8: ESP1.pin_27, Dev3.pin_8
  N9: ESP1.pin_30, Dev1.pin1, Dev2.pin2, Dev3.pin1

custom parts:
  ESP32 DOIT DEV KIT V1: The DOIT ESP32 DEV KIT V1
  GY-NEO6MV2: A GPS receiver development board with the uBlox NEO 6M chip.
  SSD1306I2C: A 128x64 pixels OLED development board with the SSD1306 chip.
  MPU9265: A MPU 9250 / 9255 development board with the 9 degree orientation sensor.
